# Fritzing sketch Sonda de temperatura Lora Covap heltec asr650x (saved by Fritzing 0.9.8b)
circuit board: 5.28174cm x 6.29cm
breadboards: 1

parts:
  Controlador = Heltec CubeCell Dev-Board [part_number=HTCC-AB01]
  J2 = screw terminal, 3 pins
  J1 = screw terminal, 4 pins
  J4 = screw terminal, 4 pins
  Vint = Screw terminal - 2 pins [package=THT]
  J7 = male pin header, 3 pins [form="♂ (male)"]
  J8 = male pin header, 3 pins [form="♂ (male)"]
  P_Solar = Screw terminal - 2 pins [package=THT]
  R3 = Resistor [tolerance=±5% power=0.25 resistance=10k package=THT]
  R2 = Resistor [tolerance=±5% power=0.25 resistance=10k package=THT]
  R4 = Resistor [tolerance=±5% power=0.25 resistance=220 package=THT]
  J10 = female pin header, 4 pins [form="♀ (female)"]
  R5 = Resistor [tolerance=±5% power=0.25 resistance=220 package=THT]
  R6 = Resistor [tolerance=±5% power=0.25 resistance=220 package=THT]
  J9 = screw terminal, 8 pins

nets:
  N1: Controlador.pin1, J8.pin3, R4.Pin_1, R5.Pin_1, R6.Pin_0, R6.Pin_1, J9.pin8
  N2: Controlador.pin2, J10.pin4, J9.pin6
  N3: Controlador.pin3, J8.pin1, J10.pin3, J9.pin7
  N4: Controlador.pin7, J9.pin5
  N5: Controlador.pin8, J9.pin4
  N6: Controlador.pin_9, J9.pin3
  N7: Controlador.pin_10, Vint.pin2, J7.pin1, R3.Pin_0, R2.Pin_0, R5.Pin_0
  GND: Controlador.pin_11, Controlador.pin_14, Controlador.pin_18, J2.pin1, J1.pin1, J4.pin1, Vint.pin1, P_Solar.pin1, R4.Pin_0, J10.pin2, J9.pin1
  N8: Controlador.pin_15, P_Solar.pin2
  N9: Controlador.pin_17, J7.pin3
  N10: Controlador.pin_19, J1.pin3, J4.pin3, R3.Pin_1
  N11: Controlador.pin_20, J1.pin4, J4.pin4, R2.Pin_1
  N12: J2.pin2, J1.pin2, J4.pin2, J7.pin2, J10.pin1, J9.pin2
  N13: J2.pin3, J8.pin2

notes:
  +
  -
  A
  L
  D
  Vext
  Vin
  Tx
  Rx
  VDC
  7
  1
  2
  MOSI
  MISO
  SCK

custom parts:
  Heltec CubeCell Dev-Board: CubeCell is a part of the Heltec LoRa series and incorporates an ASR6501 processor and SX1262 RF transceiver with an integrated CP2102 USB to serial port interface and onboard SHT1.25 battery interface with integrated lithium battery management system supporting direct solar panel connection.
