# Fritzing sketch Adactador de sensores (saved by Fritzing 0.9.6b)
circuit board: 9.89241cm x 9.28785cm
breadboards: 1

parts:
  R1 = Resistor [tolerance=±5% resistance=10k power=0.25 package=THT]
  R2 = Resistor [tolerance=±5% resistance=10k power=0.25 package=THT]
  R3 = Resistor [tolerance=±5% resistance=10k power=0.25 package=THT]
  R4 = Resistor [tolerance=±5% resistance=10k power=0.25 package=THT]
  R5 = Resistor [tolerance=±5% resistance=10k power=0.25 package=THT]
  Componente1 = Arduino MKR1000
  DHT11_1 = screw terminal, 3 pins
  DHT11_2 = screw terminal, 3 pins
  DHT11_3 = screw terminal, 3 pins
  DHT11_4 = screw terminal, 3 pins
  DHT11_5 = screw terminal, 3 pins
  HLK-PM1 = HLK-PM01
  220_AC = screw terminal, 2 pins
  Viento_1 = screw terminal, 4 pins
  Viento_2 = screw terminal, 4 pins
  R6 = Resistor [tolerance=±5% resistance=10k power=0.25 package=THT]
  R7 = Resistor [tolerance=±5% resistance=6.8k power=0.25 package=THT]
  R8 = Resistor [tolerance=±5% resistance=10k power=0.25 package=THT]
  R9 = Resistor [tolerance=±5% resistance=6.8k power=0.25 package=THT]
  DHT11_6 = screw terminal, 3 pins
  viento_3 = screw terminal, 4 pins
  R11 = Resistor [tolerance=±5% resistance=10 power=0.25 package=THT]
  R12 = Resistor [tolerance=±5% resistance=6.8k power=0.25 package=THT]
  S1 = Pushbutton [package="[THT]"]
  LED1 = LED - 5mm [color="Red (633nm)" current=0.030 package="5 mm [THT]"]
  LED2 = LED - 5mm [color="Red (633nm)" current=0.030 package="5 mm [THT]"]
  S2 = Pushbutton [package="[THT]"]
  R13 = Resistor [tolerance=±5% resistance=10k power=0.25 package=THT]
  R14 = Resistor [tolerance=±5% resistance=10k power=0.25 package=THT]
  R15 = Resistor [tolerance=±5% resistance=220 power=0.25 package=THT]
  R16 = Resistor [tolerance=±5% resistance=220 power=0.25 package=THT]
  ZS-042_RTC1 = ZS-042 RTC Module
  R10 = Resistor [tolerance=±5% resistance=10 power=0.25 package=THT]
  24V = Screw terminal - 2 pins [package=THT]

nets:
  5V: R1.Pin_0, R2.Pin_0, R3.Pin_0, R4.Pin_0, R5.Pin_0, Componente1.5V, DHT11_1.pin2, DHT11_2.pin2, DHT11_3.pin2, DHT11_4.pin2, DHT11_5.pin2, HLK-PM1.+Vo, DHT11_6.pin2, R13.Pin_0, R14.Pin_0, ZS-042_RTC1.VCC, R10.Pin_0
  N1: R1.Pin_1, Componente1.D7, DHT11_1.pin1
  N2: R2.Pin_1, Componente1.D6, DHT11_2.pin1
  N3: R3.Pin_1, Componente1.D2_PWM, DHT11_3.pin1
  N4: R4.Pin_1, Componente1.D4_PWM, DHT11_5.pin1
  N5: R5.Pin_1, Componente1.D3_PWM, DHT11_4.pin1
  N6: Componente1.A2, S1.Pin_1, S1.Pin_2, R14.Pin_1
  N7: Componente1.A3, S2.Pin_1, S2.Pin_2, R13.Pin_1
  N8: Componente1.A4, R6.Pin_1, R7.Pin_0
  N9: Componente1.A5, R8.Pin_1, R9.Pin_0
  N10: Componente1.A6, R11.Pin_1, R12.Pin_0
  N11: Componente1.D0, R16.Pin_0
  N12: Componente1.D1, R15.Pin_0
  N13: Componente1.D5_PWM, DHT11_6.pin1, R10.Pin_1
  N14: Componente1.D11_SDA, ZS-042_RTC1.SDA
  N15: Componente1.D12_SCL, ZS-042_RTC1.SCL
  GND: Componente1.GND, DHT11_1.pin3, DHT11_2.pin3, DHT11_3.pin3, DHT11_4.pin3, DHT11_5.pin3, HLK-PM1.-Vo, Viento_1.pin4, Viento_2.pin4, R7.Pin_1, R9.Pin_1, DHT11_6.pin3, viento_3.pin4, R12.Pin_1, S1.Pin_3, S1.Pin_4, LED1.cathode, LED2.cathode, S2.Pin_3, S2.Pin_4, ZS-042_RTC1.GND, 24V.pin1
  N16: HLK-PM1.AC#0, 220_AC.pin1
  N17: HLK-PM1.AC#1, 220_AC.pin2
  N18: Viento_1.pin2, R6.Pin_0
  N19: Viento_1.pin3, Viento_2.pin3, viento_3.pin3, 24V.pin2
  N20: Viento_2.pin2, R8.Pin_0
  N21: viento_3.pin2, R11.Pin_0
  N22: LED1.anode, R15.Pin_1
  N23: LED2.anode, R16.Pin_1

notes:
  +
  -
  D
  Puertos Micro
  PCB -> Micro
  1 -> 7
  2 -> 6
  3 -> 2
  4 -> 3
  5 -> 4
  6 -> 5
  Analogicos
  1 -> 4
  2 -> 5
  3 -> 6
  Botones
  1 -> A2
  2 -> A3
  Led
  1 -> 1
  2 -> 0

custom parts:
  Arduino MKR1000: MKR1000 is a powerful board that combines the functionality of the Zero and the Wi-Fi Shield. It is the ideal solution for makers wanting to design IoT projects with minimal previous experience in networking
