# Fritzing sketch disposito silos covap (saved by Fritzing 0.9.8b)
circuit board: 14.7cm x 9.76349cm
breadboards: 1

parts:
  M1 = Arduino MKR WAN 1300
  TRS1 = Audio Jack (TRS) 3.5mm [package="4Ucon 08780 [THT]"]
  TRS2 = Audio Jack (TRS) 3.5mm [package="4Ucon 08780 [THT]"]
  ADS1115 = Adafruit ADS1115 16Bit I2C ADC [part_number="Adafruit #1085"]
  HLK-PM1 = HLK-PM01
  J1 = screw terminal, 2 pins
  RY1 = srd-05vdc-sl-c
  RY2 = srd-05vdc-sl-c
  Rele2 = screw terminal, 3 pins
  Rele1 = screw terminal, 3 pins
  Q1 = NPN-Transistor [package="TO92 [THT]"]
  Q2 = NPN-Transistor [package="TO92 [THT]"]
  R1 = Resistor [tolerance=±5% power=0.25 resistance=220 package=THT]
  R2 = Resistor [tolerance=±5% power=0.25 resistance=220 package=THT]
  D1 = Rectifier Diode [part_number=1N4001 package="300 mil [THT]"]
  D2 = Rectifier Diode [part_number=1N4001 package="300 mil [THT]"]
  X1 = DB9 Connector [package=db9]
  X2 = DB9 Connector [package=db9]
  U1 = RS232 Transceiver [package=dil16]
  C1 = Ceramic Capacitor [capacitance=1µF voltage=35V package="100 mil [THT, multilayer]"]
  C2 = Ceramic Capacitor [capacitance=1µF voltage=35V package="100 mil [THT, multilayer]"]
  C4 = Ceramic Capacitor [capacitance=1µF voltage=35V package="100 mil [THT, multilayer]"]
  R4 = Resistor [tolerance=±5% power=0.25 resistance=220 package=THT]
  R3 = Resistor [tolerance=±5% power=0.25 resistance=220 package=THT]
  J2 = screw terminal, 8 pins
  Reset = Screw terminal - 2 pins [package=THT]
  R5 = Resistor [tolerance=±5% power=0.25 resistance=220 package=THT]
  C3 = Ceramic Capacitor [capacitance=1µF voltage=35V package="100 mil [THT, multilayer]"]
  R6 = Resistor [tolerance=±5% power=0.25 resistance=220 package=THT]
  R7 = Resistor [tolerance=±5% power=0.25 resistance=220 package=THT]
  LED2 = LED - 3mm [color="Red (633nm)" current=0.030 package="3 mm [THT]"]
  LED1 = LED - 3mm [color="Red (633nm)" current=0.030 package="3 mm [THT]"]

nets:
  N1: M1.0, R1.Pin_0
  N2: M1.~1, R2.Pin_0
  N3: M1.~2, J2.pin8
  N4: M1.~3, J2.pin7
  N5: M1.~4, Reset.pin1, R5.Pin_1
  N6: M1.6, LED2.cathode
  N7: M1.7, LED1.cathode
  N8: M1.11_SDA, ADS1115.SDA
  N9: M1.12_SCL, ADS1115.SCL
  N10: M1.13_RX, R3.Pin_0
  N11: M1.14_TX, R4.Pin_0
  GND: M1.GND, ADS1115.ADDR, ADS1115.GND, HLK-PM1.-Vo, X1.5, X2.5, U1.GND, C4.0, J2.pin1, J2.pin5, R5.Pin_0
  5V: M1.5V, ADS1115.VDD, HLK-PM1.+Vo, RY1.pin_4, RY2.pin_4, D1.anode, D2.anode, U1.VCC, J2.pin2, J2.pin6, Reset.pin2, C3.1, R6.Pin_1, R7.Pin_1
  N12: TRS1.Sleeve, ADS1115.AIN2
  N13: TRS1.Ring, TRS1.Tip, ADS1115.AIN3
  N14: TRS2.Sleeve, ADS1115.AIN0
  N15: TRS2.Ring, TRS2.Tip, ADS1115.AIN1
  N16: HLK-PM1.AC#0, J1.pin2
  N17: HLK-PM1.AC#1, J1.pin1
  N18: RY1.pin_1, Q1.C, D1.cathode
  N19: RY1.pin_2, Rele1.pin3
  N20: RY1.pin_3, Rele1.pin1
  N21: RY1.pin_5, Rele1.pin2
  N22: RY2.pin_1, Q2.C, D2.cathode
  N23: RY2.pin_2, Rele2.pin3
  N24: RY2.pin_3, Rele2.pin1
  N25: RY2.pin_5, Rele2.pin2
  N26: Q1.E, Q2.E
  N27: Q1.B, R1.Pin_1
  N28: Q2.B, R2.Pin_1
  N29: X1.3, U1.T1OUT
  N30: X1.4, U1.R1IN
  N31: X2.3, U1.T2OUT
  N32: X2.4, U1.R2IN
  N33: U1.C1+, C2.1
  N34: U1.V+, C3.0
  N35: U1.C1-, C2.0
  N36: U1.C2+, C1.1
  N37: U1.C2-, C1.0
  N38: U1.V-, C4.1
  N39: U1.R2OUT, U1.R1OUT, R3.Pin_1, J2.pin4
  N40: U1.T2IN, U1.T1IN, R4.Pin_1, J2.pin3
  N41: R6.Pin_0, LED1.anode
  N42: R7.Pin_0, LED2.anode

notes:
  +
  -
  Rx
  Tx
  2
  3

custom parts:
  Arduino MKR WAN 1300: Arduino MKR WAN 1300 ,Cortex-M0 CPU with LoRa connectivity. CPU: SAMD21 Cortex-M0+ 32bit low power ARM MCU, 256 KB Flash 32K SRAM. Note: pins 28 and 29 (-VBAT and +VBAT) aren't defined in PCB view, because they are terminal blocks and don't connect to the pcb. Parts Editor will complain about unassigned pins but it is safe to ignore those 2 pins.
  Adafruit ADS1115 16Bit I2C ADC: For microcontrollers without an analog-to-digital converter or when you want a higher-precision ADC, the ADS1115 provides 16-bit precision at 860 samples/second over I2C. The chip can be configured as 4 single-ended input channels, or two differential channels. As a nice bonus, it even includes a programmable gain amplifier, up to x16, to help boost up smaller single/differential signals to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
